// Logisim project day1_logic.circ as structural Verilog: 7 circuits, main circuit main
module main (
  input  a0,
  input  b0,
  input  cin,
  input  a1,
  input  b1,
  input  a2,
  input  b2,
  input  a3,
  input  b3,
  output out_10
);

  wire [3:0] fourbitadder_1_s0;

  FourBitAdder fourbitadder_1 (
    .a0(a0), .b0(b0), .cin(cin), .a1(a1), .b1(b1), .a2(a2), .b2(b2), .a3(a3), .b3(b3),
    .s0(fourbitadder_1_s0[0]), .s1(fourbitadder_1_s0[1]), .s2(fourbitadder_1_s0[2]),
    .s3(fourbitadder_1_s0[3]), .cout(out_10));
  Hex_Digit_Display hex_digit_display_1 (.value(fourbitadder_1_s0));  // open: dp
endmodule

module OneBitAdder (
  input  a,
  input  b,
  input  c,
  output s,
  output cout
);

  wire AB_out, AC_out, BC_out;

  and AB (AB_out, b, a);
  and BC (BC_out, c, b);
  and AC (AC_out, c, a);
  xor xor_1 (s, c, b, a);
  or or_1 (cout, AB_out, BC_out, AC_out);
endmodule

module FourBitAdder (
  input  a0,
  input  b0,
  input  cin,
  input  a1,
  input  b1,
  input  a2,
  input  b2,
  input  a3,
  input  b3,
  output s0,
  output s1,
  output s2,
  output s3,
  output cout
);

  wire onebitadder_1_cout, onebitadder_2_cout, onebitadder_3_cout;

  OneBitAdder onebitadder_1 (.a(a0), .b(b0), .c(cin), .s(s0), .cout(onebitadder_1_cout));
  OneBitAdder onebitadder_2 (.a(a1), .b(b1), .c(onebitadder_1_cout), .s(s1), .cout(onebitadder_2_cout));
  OneBitAdder onebitadder_3 (.a(a2), .b(b2), .c(onebitadder_2_cout), .s(s2), .cout(onebitadder_3_cout));
  OneBitAdder onebitadder_4 (.a(a3), .b(b3), .c(onebitadder_3_cout), .s(s3), .cout(cout));
endmodule

module OneBitAddSub (
  input  binv,
  input  a,
  input  b,
  input  cin,
  output s,
  output cout
);

  wire multiplexer_1_out, not_1_out;

  not not_1 (not_1_out, b);
  Multiplexer multiplexer_1 (.in0(b), .in1(not_1_out), .out(multiplexer_1_out), .sel(binv));
  OneBitAdder onebitadder_1 (.a(a), .b(multiplexer_1_out), .c(cin), .s(s), .cout(cout));
endmodule

module FourBitAddSub (
  input  sub,
  input  a0,
  input  b0,
  input  a1,
  input  b1,
  input  a2,
  input  b2,
  input  a3,
  input  b3,
  output out_10
);

  wire onebitaddsub_1_cout, onebitaddsub_2_cout, onebitaddsub_3_cout;
  wire [3:0] onebitaddsub_1_s;

  OneBitAddSub onebitaddsub_1 (
    .binv(sub), .a(a0), .b(b0), .cin(sub), .s(onebitaddsub_1_s[0]), .cout(onebitaddsub_1_cout));
  OneBitAddSub onebitaddsub_2 (
    .binv(sub), .a(a1), .b(b1), .cin(onebitaddsub_1_cout), .s(onebitaddsub_1_s[1]), .cout(onebitaddsub_2_cout));
  OneBitAddSub onebitaddsub_3 (
    .binv(sub), .a(a2), .b(b2), .cin(onebitaddsub_2_cout), .s(onebitaddsub_1_s[2]), .cout(onebitaddsub_3_cout));
  OneBitAddSub onebitaddsub_4 (
    .binv(sub), .a(a3), .b(b3), .cin(onebitaddsub_3_cout), .s(onebitaddsub_1_s[3]), .cout(out_10));
  Hex_Digit_Display hex_digit_display_1 (.value(onebitaddsub_1_s));  // open: dp
endmodule

module RS_latch (
  input  S,
  input  R,
  output Q,
  output Qnot
);

  nand nand_1 (Q, S, Qnot);
  nand nand_2 (Qnot, Q, R);

  // Notes on the sheet:
  //   Cross coupled nand gates
endmodule

module D_latch (
  input  D,
  input  WE,
  output out_3
);

  wire nand_1_out, nand_2_out;

  nand nand_1 (nand_1_out, D, WE);
  nand nand_2 (nand_2_out, WE, ~D);  // NAND_Gate
  RS_latch rs_latch_1 (.S(nand_1_out), .R(nand_2_out), .Q(out_3));  // open: Qnot

  // Notes on the sheet:
  //   D high-level triggered latch
  //   WE = 0 Q is unchanged or constant
endmodule
